// Logisim project CPU.circ as structural Verilog: 8 circuits, main circuit main
module main (
  output [9:0] out_1,
  output [9:0] out_2,
  output [9:0] out_3,
  output [9:0] out_4,
  output [9:0] out_5,
  output [9:0] out_6,
  output [9:0] out_7,
  output ignore,
  output halt,
  output [4:0] out_10,
  output [4:0] out_11,
  output [4:0] out_12,
  output [9:0] out_13,
  output [4:0] out_14,
  output [9:0] out_15,
  output [9:0] out_16,
  output [9:0] out_17
);

  wire and_1_out, and_2_out, and_3_out, and_6_out, and_7_out, CLK, clock_1_out, comparator_1_lt,
       comparator_2_lt, not_1_out, not_2_out, not_3_out, not_4_out, not_6_out, not_7_out, not_8_out,
       not_9_out, not_10_out, not_11_out, not_12_out, not_13_out, not_14_out, not_15_out, or_1_out, or_2_out,
       t_ff_1_q, TClock;
  wire [1:0] counter_2_q, nor_1_out, Upper_2_bits;
  wire [1:1] and_4_out, not_5_out;
  wire [2:0] A_ADDR, B_ADDR, DEST, multiplexer_2_out, multiplexer_3_out, multiplexer_5_out, rom_1_data;
  wire [4:0] counter_1_q;
  wire [6:0] adder_1_out, adder_2_out, ASCII, LSB, MiddleBits;
  wire [7:0] multiplexer_4_out;
  wire [9:0] multiplexer_7_out, multiplexer_9_out;
  wire [23:19] ram_1_data;

  Multiplexer #(.width(5)) multiplexer_1 (
    .in0(5'b00001), .in1(out_13[4:0]), .out(out_12), .sel(and_1_out));  // open: en
  or or_1 (or_1_out, out_17[9], out_17[8], out_17[7], out_17[6], out_17[5], out_17[4], out_17[3], out_17[2], out_17[1], out_17[0]);
  RAM #(.addrWidth(5), .dataWidth(24), .bus("separate")) ram_1 (
    .addr(out_10), .data({ram_1_data, DEST, A_ADDR, B_ADDR, out_13}));  // open: din, str, sel, clk, ld, clr
  PC pc_1 (.INPUT(out_11), .SELECTOR(not_1_out), .CLOCK(CLK), .OUTPUT(out_10));
  PC_A_S pc_a_s_1 (.B(out_12), .A(out_10), .PC_AS_OUT(out_11));
  not not_1 (not_1_out, and_3_out);
  and and_1 (and_1_out, or_1_out, nor_1_out[1]);
  not not_2 (not_2_out, ram_1_data[19]);
  not not_3 (not_3_out, ram_1_data[20]);
  not not_4 (not_4_out, ram_1_data[23]);
  not not_5 (not_5_out[1], ram_1_data[23]);
  not not_6 (not_6_out, ram_1_data[21]);
  not not_7 (not_7_out, ram_1_data[23]);
  not not_8 (not_8_out, ram_1_data[21]);
  not not_9 (not_9_out, ram_1_data[23]);
  not not_10 (not_10_out, ram_1_data[19]);
  not not_11 (not_11_out, ram_1_data[21]);
  not not_12 (not_12_out, ram_1_data[23]);
  nor nor_1 (nor_1_out[0], ram_1_data[22], ram_1_data[23]);
  and and_2 (and_2_out, not_2_out, not_3_out, ram_1_data[21], ram_1_data[22], not_4_out);
  and and_3 (and_3_out, ram_1_data[19], ram_1_data[20], ram_1_data[21], ram_1_data[22], ram_1_data[23]);
  and and_4 (and_4_out[1], ram_1_data[20], not_6_out, ram_1_data[22], not_7_out);
  and and_5 (nor_1_out[1], ram_1_data[19], ram_1_data[20], not_8_out, ram_1_data[22], not_9_out);
  and and_6 (and_6_out, not_10_out, ram_1_data[20], not_11_out, ram_1_data[22], not_12_out);
  Multiplexer #(.width(3)) multiplexer_2 (
    .in0(multiplexer_3_out), .in1(ram_1_data[21:19]), .out(multiplexer_2_out), .sel(nor_1_out[0]));  // open: en
  TTY #(.rows(33), .cols(4)) tty_1 (.data(ASCII), .clk(TClock));  // open: we, clr
  or or_2 (or_2_out, nor_1_out[1], and_2_out, and_3_out);
  not not_13 (not_13_out, or_2_out);
  Multiplexer #(.select(2), .width(3)) multiplexer_3 (
    .in0({ram_1_data[23], {2{not_5_out[1]}}}), .in1({3{not_5_out[1]}}),
    .in2({not_5_out[1], {2{ram_1_data[23]}}}), .in3({{2{ram_1_data[23]}}, not_5_out[1]}),
    .out(multiplexer_3_out), .sel({and_4_out[1], ram_1_data[19]}));  // open: en
  not not_14 (not_14_out, and_6_out);
  // Probe on out_1
  // Probe on out_5
  Counter #(.width(5), .max('h1f), .ongoal("stay")) counter_1 (
    .Q(counter_1_q), .carry(halt), .clk(CLK));  // open: load, D, count, clr
  // Probe on out_2
  // Probe on out_6
  Multiplexer #(.select(3), .width(10)) multiplexer_4 (
    .in0(out_1), .in1(out_2), .in2(out_3), .in3(out_4), .in4(out_5), .in5(out_6), .in6(out_7),
    .out({Upper_2_bits, multiplexer_4_out}), .sel(rom_1_data));  // open: in7, en
  not not_15 (not_15_out, halt);
  Clock clock_1 (.out(clock_1_out));
  Multiplexer #(.width(3)) multiplexer_5 (
    .in0(A_ADDR), .in1(DEST), .out(multiplexer_5_out), .sel(nor_1_out[1]));  // open: en
  Multiplexer #(.select(3), .width(10)) multiplexer_6 (
    .in0(out_1), .in1(out_2), .in2(out_3), .in3(out_4), .in4(out_5), .in5(out_6), .in6(out_7), .out(out_16),
    .sel(multiplexer_5_out));  // open: in7, en
  Multiplexer #(.width(10)) multiplexer_7 (
    .in0(out_13), .in1(out_16), .out(multiplexer_7_out), .sel(not_14_out));  // open: en
  // Probe on out_3
  // Probe on out_7
  ROM #(.addrWidth(5), .dataWidth(3)) rom_1 (.addr(counter_1_q), .data(rom_1_data));  // open: sel
  and and_7 (and_7_out, not_15_out, clock_1_out);
  not not_16 (TClock, and_7_out);
  T_Flip_Flop t_ff_1 (.clk(and_7_out), .T(1'b1), .Q(t_ff_1_q));  // open: Qn, preset, reset, en
  ALU alu_1 (
    .ALU_OUT(out_17), .B(multiplexer_9_out), .A(multiplexer_7_out), .ALU_S2(multiplexer_2_out[2]),
    .ALU_S1(multiplexer_2_out[1]), .ALU_S0(multiplexer_2_out[0]));
  // Probe on out_4
  Comparator #(.width(7)) comparator_1 (
    .a(7'b0111001), .b({3'b011, multiplexer_4_out[3:0]}), .lt(comparator_1_lt));  // open: gt, eq
  Comparator #(.width(7)) comparator_2 (
    .a(7'b0111001), .b({3'b011, multiplexer_4_out[7:4]}), .lt(comparator_2_lt));  // open: gt, eq
  T_Flip_Flop t_ff_2 (.clk(t_ff_1_q), .T(1'b1), .Q(CLK));  // open: Qn, preset, reset, en
  Multiplexer #(.select(3), .width(10)) multiplexer_8 (
    .in0(out_1), .in1(out_2), .in2(out_3), .in3(out_4), .in4(out_5), .in5(out_6), .in6(out_7), .out(out_15),
    .sel(B_ADDR));  // open: in7, en
  Multiplexer #(.select(2), .width(10)) multiplexer_9 (
    .in0(out_13), .in1(out_15), .in2({10{1'b0}}), .out(multiplexer_9_out), .sel(nor_1_out));  // open: in3, en
  Adder #(.width(7)) adder_1 (
    .a({3'b011, multiplexer_4_out[3:0]}), .b(7'b0000111), .out(adder_1_out));  // open: cin, cout
  Adder #(.width(7)) adder_2 (
    .a({3'b011, multiplexer_4_out[7:4]}), .b(7'b0000111), .out(adder_2_out));  // open: cin, cout
  Multiplexer #(.select(2), .width(7)) multiplexer_10 (
    .in0({5'b01100, Upper_2_bits}), .in1(MiddleBits), .in2(LSB), .in3(7'b0100000), .out(ASCII),
    .sel(counter_2_q));  // open: en
  Counter #(.width(2), .max('h3)) counter_2 (.Q(counter_2_q), .clk(TClock));  // open: load, D, count, carry, clr
  Multiplexer #(.width(7), .disabled(0), .enable("false")) multiplexer_11 (
    .in0({3'b011, multiplexer_4_out[3:0]}), .in1(adder_1_out), .out(LSB), .sel(comparator_1_lt));
  Multiplexer #(.width(7), .disabled(0), .enable("false")) multiplexer_12 (
    .in0({3'b011, multiplexer_4_out[7:4]}), .in1(adder_2_out), .out(MiddleBits), .sel(comparator_2_lt));
  T_Flip_Flop t_ff_3 (.clk(CLK), .T(1'b1), .Q(ignore));  // open: Qn, preset, reset, en
  Register_Bank register_bank_1 (
    .WRITE_OR_NOT(not_13_out), .Write_Val(out_17), .CLOCK(CLK), .Destination_Address(DEST), .R0(out_1),
    .R1(out_2), .R2(out_3), .R3(out_4), .R4(out_5), .R5(out_6), .R6(out_7));

  assign out_14 = out_10;

  // Other names for the same wires on the sheet: DATA[9:0] = out_13; BNEZ[9:0] = out_17; R0[9:0] = out_1;
  //   R1[9:0] = out_2; R2[9:0] = out_3; R3[9:0] = out_4; R4[9:0] = out_5; R5[9:0] = out_6; R6[9:0] = out_7

  // Notes on the sheet:
  //   Double click on the subcircuits
  //   to the right to see how they work.
  //   RAM
  //   1. Press ctrl-r to reset.
  //   Scroll down for instructions.
  //   3. Press ctrl-k to start the simulation.
  //   2. Right-click on the RAM above > Load Image > test.txt > open
  //   DATA
  //   B ADDRESS
  //   A ADDRESS
  //   DEST ADDR
  //   OP CODE
  //   NOTE: You may change the speed of the simulation by clicking Simulate > Tick Frequency
  //   If the output from the tester matches
  //   the text on the left of the gray area,
  //   then the CPU is working properly.
  //   34F
  //   0F5
  //   1EA
  //   07A
  //   29B
  //   165
  //   10F
  //   0F5
  //   0AA
  //   0AA
  //   05A
  //   00A
  //   0FA
  //   104
  //   0B4
  //   165
  //   165
  //   001
  //   001
  //   000
  //   000
  //   000
  //   000
  //   000
  //   ???
  //   CPU
  //   0F5
  //   0F5
  //   25A
  //   050
  //   2FF
  //   30A
  //   contents of rom_1 (hex, n*v repeats v):
  //   0 0 0 1 2 3 4 5 6 2 3 4 5 6 0 0 0 1 3 4 6 3 5 5 8*6
  //   A
  //   TESTER
  //   B
endmodule

// AONA
module AND_OR_NOT_ADD (
  input  CIN,
  input  A0,
  input  B0,
  input  S1,
  input  S0,
  input  A1,
  input  B1,
  input  A2,
  input  B2,
  input  A3,
  input  B3,
  input  A4,
  input  B4,
  input  A5,
  input  B5,
  input  A6,
  input  B6,
  input  A7,
  input  B7,
  input  A8,
  input  B8,
  input  A9,
  input  B9,
  output C0,
  output C1,
  output C2,
  output C3,
  output C4,
  output C5,
  output C6,
  output C7,
  output C8,
  output C9,
  output COUT
);

  wire and_1_out, and_2_out, and_3_out, and_4_out, and_5_out, and_6_out, and_7_out, and_8_out, and_9_out,
       and_10_out, and_11_out, and_12_out, and_13_out, and_14_out, and_15_out, and_16_out, and_17_out,
       and_18_out, and_19_out, and_20_out, and_21_out, and_22_out, and_23_out, and_24_out, and_25_out,
       and_26_out, and_27_out, and_28_out, and_29_out, and_30_out, G0_2_out, G0_out, G1_2_out, G1_out,
       G2_2_out, G2_out, G3_2_out, G3_out, G4_2_out, G4_out, not_1_out, not_2_out, not_3_out, not_4_out,
       not_5_out, not_6_out, not_7_out, not_8_out, not_9_out, not_10_out, OR0_2_out, OR0_out, OR1_2_out,
       OR1_out, OR2_2_out, OR2_out, OR3_2_out, OR3_out, OR4_2_out, OR4_out, or_1_out, or_2_out, or_3_out,
       or_4_out, or_5_out, or_6_out, or_7_out, or_8_out, or_9_out, P0_2_out, P0_out, P1_2_out, P1_out,
       P2_2_out, P2_out, P3_2_out, P3_out, P4_2_out, P4_out, sum0_2_out, sum0_out, sum1_2_out, sum1_out,
       sum2_2_out, sum2_out, sum3_2_out, sum3_out, sum4_2_out, sum4_out;

  xor P0 (P0_out, A0, B0);
  and G0 (G0_out, A0, B0);
  xor P1 (P1_out, A1, B1);
  and G1 (G1_out, A1, B1);
  xor P2 (P2_out, A2, B2);
  and G2 (G2_out, A2, B2);
  xor P3 (P3_out, A3, B3);
  and G3 (G3_out, A3, B3);
  xor P4 (P4_out, A4, B4);
  and G4 (G4_out, A4, B4);
  and G0_2 (G0_2_out, A5, B5);
  and G1_2 (G1_2_out, A6, B6);
  and G2_2 (G2_2_out, A7, B7);
  and G3_2 (G3_2_out, A8, B8);
  and G4_2 (G4_2_out, A9, B9);
  xor P0_2 (P0_2_out, A5, B5);
  xor P1_2 (P1_2_out, A6, B6);
  xor P2_2 (P2_2_out, A7, B7);
  xor P3_2 (P3_2_out, A8, B8);
  xor P4_2 (P4_2_out, A9, B9);
  not not_1 (not_1_out, A0);
  not not_2 (not_2_out, A1);
  not not_3 (not_3_out, A2);
  not not_4 (not_4_out, A3);
  not not_5 (not_5_out, A4);
  not not_6 (not_6_out, A5);
  not not_7 (not_7_out, A6);
  not not_8 (not_8_out, A7);
  not not_9 (not_9_out, A8);
  not not_10 (not_10_out, A9);
  xor sum0 (sum0_out, CIN, P0_out);
  or OR0 (OR0_out, A0, B0);
  xor sum1 (sum1_out, or_1_out, P1_out);
  or OR1 (OR1_out, A1, B1);
  xor sum2 (sum2_out, or_2_out, P2_out);
  or OR2 (OR2_out, A2, B2);
  xor sum3 (sum3_out, or_3_out, P3_out);
  or OR3 (OR3_out, A3, B3);
  xor sum4 (sum4_out, or_7_out, P4_out);
  or OR4 (OR4_out, A4, B4);
  xor sum0_2 (sum0_2_out, or_8_out, P0_2_out);
  or OR0_2 (OR0_2_out, A5, B5);
  xor sum1_2 (sum1_2_out, or_4_out, P1_2_out);
  or OR1_2 (OR1_2_out, A6, B6);
  xor sum2_2 (sum2_2_out, or_5_out, P2_2_out);
  or OR2_2 (OR2_2_out, A7, B7);
  xor sum3_2 (sum3_2_out, or_6_out, P3_2_out);
  or OR3_2 (OR3_2_out, A8, B8);
  xor sum4_2 (sum4_2_out, or_9_out, P4_2_out);
  or OR4_2 (OR4_2_out, A9, B9);
  Multiplexer #(.select(2)) multiplexer_1 (
    .in0(G0_out), .in1(OR0_out), .in2(not_1_out), .in3(sum0_out), .out(C0), .sel({S1, S0}));  // open: en
  Multiplexer #(.select(2)) multiplexer_2 (
    .in0(G1_out), .in1(OR1_out), .in2(not_2_out), .in3(sum1_out), .out(C1), .sel({S1, S0}));  // open: en
  Multiplexer #(.select(2)) multiplexer_3 (
    .in0(G2_out), .in1(OR2_out), .in2(not_3_out), .in3(sum2_out), .out(C2), .sel({S1, S0}));  // open: en
  Multiplexer #(.select(2)) multiplexer_4 (
    .in0(G3_out), .in1(OR3_out), .in2(not_4_out), .in3(sum3_out), .out(C3), .sel({S1, S0}));  // open: en
  Multiplexer #(.select(2)) multiplexer_5 (
    .in0(G4_out), .in1(OR4_out), .in2(not_5_out), .in3(sum4_out), .out(C4), .sel({S1, S0}));  // open: en
  Multiplexer #(.select(2)) multiplexer_6 (
    .in0(G0_2_out), .in1(OR0_2_out), .in2(not_6_out), .in3(sum0_2_out), .out(C5), .sel({S1, S0}));  // open: en
  Multiplexer #(.select(2)) multiplexer_7 (
    .in0(G1_2_out), .in1(OR1_2_out), .in2(not_7_out), .in3(sum1_2_out), .out(C6), .sel({S1, S0}));  // open: en
  Multiplexer #(.select(2)) multiplexer_8 (
    .in0(G2_2_out), .in1(OR2_2_out), .in2(not_8_out), .in3(sum2_2_out), .out(C7), .sel({S1, S0}));  // open: en
  Multiplexer #(.select(2)) multiplexer_9 (
    .in0(G3_2_out), .in1(OR3_2_out), .in2(not_9_out), .in3(sum3_2_out), .out(C8), .sel({S1, S0}));  // open: en
  Multiplexer #(.select(2)) multiplexer_10 (
    .in0(G4_2_out), .in1(OR4_2_out), .in2(not_10_out), .in3(sum4_2_out), .out(C9), .sel({S1, S0}));  // open: en
  and and_1 (and_1_out, P0_out, CIN);
  and and_2 (and_2_out, G0_out, P1_out);
  and and_3 (and_3_out, P1_out, P0_out, CIN);
  and and_4 (and_4_out, P2_out, G1_out);
  and and_5 (and_5_out, P2_out, P1_out, G0_out);
  and and_6 (and_6_out, P2_out, P1_out, CIN, P0_out);
  and and_7 (and_7_out, P0_2_out, or_8_out);
  and and_8 (and_8_out, G0_2_out, P1_2_out);
  and and_9 (and_9_out, P1_2_out, P0_2_out, or_8_out);
  and and_10 (and_10_out, P2_2_out, G1_2_out);
  and and_11 (and_11_out, P2_2_out, P1_2_out, G0_2_out);
  and and_12 (and_12_out, P2_2_out, P1_2_out, or_8_out, P0_2_out);
  or or_1 (or_1_out, and_1_out, G0_out);
  or or_2 (or_2_out, and_2_out, G1_out, and_3_out);
  or or_3 (or_3_out, and_4_out, G2_out, and_6_out, and_5_out);
  or or_4 (or_4_out, and_7_out, G0_2_out);
  or or_5 (or_5_out, and_8_out, G1_2_out, and_9_out);
  or or_6 (or_6_out, and_10_out, G2_2_out, and_12_out, and_11_out);
  and and_13 (and_13_out, P4_out, G3_out);
  and and_14 (and_14_out, P4_out, P3_out, G2_out);
  and and_15 (and_15_out, P4_out, P3_out, P2_out, G1_out);
  and and_16 (and_16_out, P4_out, P3_out, P2_out, P1_out, G0_out);
  and and_17 (and_17_out, P4_out, P3_out, P2_out, P1_out, P0_out, CIN);
  and and_18 (and_18_out, P3_out, G2_out);
  and and_19 (and_19_out, P3_out, P2_out, G1_out);
  and and_20 (and_20_out, P3_out, P2_out, P1_out, G0_out);
  and and_21 (and_21_out, P3_out, P2_out, P1_out, P0_out, CIN);
  and and_22 (and_22_out, P3_2_out, G2_2_out);
  and and_23 (and_23_out, P3_2_out, P2_2_out, G1_2_out);
  and and_24 (and_24_out, P3_2_out, P2_2_out, P1_2_out, G0_2_out);
  and and_25 (and_25_out, P3_2_out, P2_2_out, P1_2_out, P0_2_out, or_8_out);
  and and_26 (and_26_out, P4_2_out, G3_2_out);
  and and_27 (and_27_out, P4_2_out, P3_2_out, G2_2_out);
  and and_28 (and_28_out, P4_2_out, P3_2_out, P2_2_out, G1_2_out);
  and and_29 (and_29_out, P4_2_out, P3_2_out, P2_2_out, P1_2_out, G0_2_out);
  and and_30 (and_30_out, P4_2_out, P3_2_out, P2_2_out, P1_2_out, P0_2_out, or_8_out);
  or or_7 (or_7_out, and_18_out, and_19_out, G3_out, and_21_out, and_20_out);
  or or_8 (or_8_out, G4_out, and_13_out, and_14_out, and_16_out, and_15_out, and_17_out);
  or or_9 (or_9_out, and_22_out, and_23_out, G3_2_out, and_25_out, and_24_out);
  or or_10 (COUT, G4_2_out, and_26_out, and_27_out, and_29_out, and_28_out, and_30_out);
endmodule

module ALU (
  input  [9:0] B,
  input  [9:0] A,
  input  ALU_S2,
  input  ALU_S1,
  input  ALU_S0,
  output [9:0] ALU_OUT
);

  wire and_or_not_add_2_cout, not_1_out;
  wire [9:0] and_or_not_add_1_c0, and_or_not_add_2_c0, multiplexer_1_out, shift_1_shift_l_out,
       shift_1_shift_r_out;

  AND_OR_NOT_ADD and_or_not_add_1 (
    .A0(B[0]), .A1(B[1]), .A2(B[2]), .A3(B[3]), .A4(B[4]), .A5(B[5]), .A6(B[6]), .A7(B[7]), .A8(B[8]),
    .A9(B[9]), .S1(ALU_S2), .S0(not_1_out), .C0(and_or_not_add_1_c0[0]), .C1(and_or_not_add_1_c0[1]),
    .C2(and_or_not_add_1_c0[2]), .C3(and_or_not_add_1_c0[3]), .C4(and_or_not_add_1_c0[4]),
    .C5(and_or_not_add_1_c0[5]), .C6(and_or_not_add_1_c0[6]), .C7(and_or_not_add_1_c0[7]),
    .C8(and_or_not_add_1_c0[8]), .C9(and_or_not_add_1_c0[9]));  // open: CIN, B0, B1, B2, B3, B4, B5, B6, B7, B8, B9, COUT
  Multiplexer #(.width(10)) multiplexer_1 (
    .in0(B), .in1(and_or_not_add_1_c0), .out(multiplexer_1_out), .sel(ALU_S2));  // open: en
  not not_1 (not_1_out, ALU_S2);
  SHIFT shift_1 (.SHIFT_R_OUT(shift_1_shift_r_out), .SHIFT_L_OUT(shift_1_shift_l_out), .DATA(A));
  Multiplexer #(.select(3), .width(10)) multiplexer_2 (
    .in0(and_or_not_add_2_c0), .in1(and_or_not_add_2_c0), .in2(and_or_not_add_2_c0),
    .in3(and_or_not_add_2_c0), .in4(A), .in5(shift_1_shift_l_out), .in6(shift_1_shift_r_out),
    .in7(and_or_not_add_2_c0), .out(ALU_OUT), .sel({ALU_S2, ALU_S1, ALU_S0}));  // open: en
  AND_OR_NOT_ADD and_or_not_add_2 (
    .CIN(ALU_S2), .A0(A[0]), .B0(multiplexer_1_out[0]), .A1(A[1]), .B1(multiplexer_1_out[1]), .A2(A[2]),
    .B2(multiplexer_1_out[2]), .A3(A[3]), .B3(multiplexer_1_out[3]), .A4(A[4]), .B4(multiplexer_1_out[4]),
    .A5(A[5]), .B5(multiplexer_1_out[5]), .A6(A[6]), .B6(multiplexer_1_out[6]), .A7(A[7]),
    .B7(multiplexer_1_out[7]), .A8(A[8]), .B8(multiplexer_1_out[8]), .A9(A[9]), .B9(multiplexer_1_out[9]),
    .COUT(and_or_not_add_2_cout), .S1(ALU_S1), .S0(ALU_S0), .C0(and_or_not_add_2_c0[0]),
    .C1(and_or_not_add_2_c0[1]), .C2(and_or_not_add_2_c0[2]), .C3(and_or_not_add_2_c0[3]),
    .C4(and_or_not_add_2_c0[4]), .C5(and_or_not_add_2_c0[5]), .C6(and_or_not_add_2_c0[6]),
    .C7(and_or_not_add_2_c0[7]), .C8(and_or_not_add_2_c0[8]), .C9(and_or_not_add_2_c0[9]));

  // Notes on the sheet:
  //   B
  //   ~B
  //   A
endmodule

module SHIFT (
  input  [9:0] DATA,
  output [9:0] SHIFT_R_OUT,
  output [9:0] SHIFT_L_OUT
);

  wire not_1_out;

  not not_1 (not_1_out, DATA[9]);
  and and_1 (SHIFT_L_OUT[0], DATA[9], not_1_out);

  assign SHIFT_L_OUT[9:1] = DATA[8:0];
  assign SHIFT_R_OUT = {SHIFT_L_OUT[0], DATA[9:1]};
endmodule

module Register (
  input  CHANGE_SELECTOR,
  input  CLOCK,
  input  [9:0] \input ,
  output [9:0] \output 
);

  wire multiplexer_1_out, multiplexer_2_out, multiplexer_3_out, multiplexer_4_out, multiplexer_5_out,
       multiplexer_6_out, multiplexer_7_out, multiplexer_8_out, multiplexer_9_out, multiplexer_10_out;

  Multiplexer multiplexer_1 (
    .in0(\output [0]), .in1(\input [0]), .out(multiplexer_1_out), .sel(CHANGE_SELECTOR));  // open: en
  Multiplexer multiplexer_2 (
    .in0(\output [1]), .in1(\input [1]), .out(multiplexer_2_out), .sel(CHANGE_SELECTOR));  // open: en
  Multiplexer multiplexer_3 (
    .in0(\output [2]), .in1(\input [2]), .out(multiplexer_3_out), .sel(CHANGE_SELECTOR));  // open: en
  Multiplexer multiplexer_4 (
    .in0(\output [3]), .in1(\input [3]), .out(multiplexer_4_out), .sel(CHANGE_SELECTOR));  // open: en
  Multiplexer multiplexer_5 (
    .in0(\output [4]), .in1(\input [4]), .out(multiplexer_5_out), .sel(CHANGE_SELECTOR));  // open: en
  Multiplexer multiplexer_6 (
    .in0(\output [5]), .in1(\input [5]), .out(multiplexer_6_out), .sel(CHANGE_SELECTOR));  // open: en
  Multiplexer multiplexer_7 (
    .in0(\output [6]), .in1(\input [6]), .out(multiplexer_7_out), .sel(CHANGE_SELECTOR));  // open: en
  Multiplexer multiplexer_8 (
    .in0(\output [7]), .in1(\input [7]), .out(multiplexer_8_out), .sel(CHANGE_SELECTOR));  // open: en
  Multiplexer multiplexer_9 (
    .in0(\output [8]), .in1(\input [8]), .out(multiplexer_9_out), .sel(CHANGE_SELECTOR));  // open: en
  Multiplexer multiplexer_10 (
    .in0(\output [9]), .in1(\input [9]), .out(multiplexer_10_out), .sel(CHANGE_SELECTOR));  // open: en
  D_Flip_Flop B0 (.clk(CLOCK), .D(multiplexer_1_out), .Q(\output [0]));  // open: Qn, preset, en, reset
  D_Flip_Flop B1 (.clk(CLOCK), .D(multiplexer_2_out), .Q(\output [1]));  // open: Qn, preset, en, reset
  D_Flip_Flop B2 (.clk(CLOCK), .D(multiplexer_3_out), .Q(\output [2]));  // open: Qn, preset, en, reset
  D_Flip_Flop B3 (.clk(CLOCK), .D(multiplexer_4_out), .Q(\output [3]));  // open: Qn, preset, en, reset
  D_Flip_Flop B4 (.clk(CLOCK), .D(multiplexer_5_out), .Q(\output [4]));  // open: Qn, preset, en, reset
  D_Flip_Flop B5 (.clk(CLOCK), .D(multiplexer_6_out), .Q(\output [5]));  // open: Qn, preset, en, reset
  D_Flip_Flop B6 (.clk(CLOCK), .D(multiplexer_7_out), .Q(\output [6]));  // open: Qn, preset, en, reset
  D_Flip_Flop B7 (.clk(CLOCK), .D(multiplexer_8_out), .Q(\output [7]));  // open: Qn, preset, en, reset
  D_Flip_Flop B8 (.clk(CLOCK), .D(multiplexer_9_out), .Q(\output [8]));  // open: Qn, preset, en, reset
  D_Flip_Flop B9 (.clk(CLOCK), .D(multiplexer_10_out), .Q(\output [9]));  // open: Qn, preset, en, reset
endmodule

module Register_Bank (
  input  [2:0] Destination_Address,
  input  WRITE_OR_NOT,
  input  CLOCK,
  input  [9:0] Write_Val,
  output [9:0] R0,
  output [9:0] R1,
  output [9:0] R2,
  output [9:0] R3,
  output [9:0] R4,
  output [9:0] R5,
  output [9:0] R6
);

  wire and_1_out, demultiplexer_1_out0, demultiplexer_1_out1, demultiplexer_1_out2, demultiplexer_1_out3,
       demultiplexer_1_out4, demultiplexer_1_out5, demultiplexer_1_out6, multiplexer_1_out, not_1_out,
       not_2_out;

  and and_1 (and_1_out, CLOCK, not_1_out);
  not not_1 (not_1_out, CLOCK);
  not not_2 (not_2_out, and_1_out);
  Multiplexer multiplexer_1 (
    .in0(and_1_out), .in1(not_2_out), .out(multiplexer_1_out), .sel(WRITE_OR_NOT));  // open: en
  Register register_1 (.\input (Write_Val), .CHANGE_SELECTOR(demultiplexer_1_out0), .CLOCK(CLOCK), .\output (R0));
  Register register_2 (.\input (Write_Val), .CHANGE_SELECTOR(demultiplexer_1_out1), .CLOCK(CLOCK), .\output (R1));
  Register register_3 (.\input (Write_Val), .CHANGE_SELECTOR(demultiplexer_1_out2), .CLOCK(CLOCK), .\output (R2));
  Register register_4 (.\input (Write_Val), .CHANGE_SELECTOR(demultiplexer_1_out3), .CLOCK(CLOCK), .\output (R3));
  Register register_5 (.\input (Write_Val), .CHANGE_SELECTOR(demultiplexer_1_out4), .CLOCK(CLOCK), .\output (R4));
  Register register_6 (.\input (Write_Val), .CHANGE_SELECTOR(demultiplexer_1_out5), .CLOCK(CLOCK), .\output (R5));
  Register register_7 (.\input (Write_Val), .CHANGE_SELECTOR(demultiplexer_1_out6), .CLOCK(CLOCK), .\output (R6));
  Demultiplexer #(.select(3)) demultiplexer_1 (
    .out0(demultiplexer_1_out0), .out1(demultiplexer_1_out1), .out2(demultiplexer_1_out2),
    .out3(demultiplexer_1_out3), .out4(demultiplexer_1_out4), .out5(demultiplexer_1_out5),
    .out6(demultiplexer_1_out6), .in(multiplexer_1_out), .sel(Destination_Address));  // open: out7, en
endmodule

module PC_A_S (
  input  [4:0] B,
  input  [4:0] A,
  output [4:0] PC_AS_OUT
);

  AND_OR_NOT_ADD and_or_not_add_1 (
    .CIN(1'b0), .A0(A[0]), .B0(B[0]), .A1(A[1]), .B1(B[1]), .A2(A[2]), .B2(B[2]), .A3(A[3]), .B3(B[3]),
    .A4(A[4]), .B4(B[4]), .S1(1'b1), .S0(1'b1), .C0(PC_AS_OUT[0]), .C1(PC_AS_OUT[1]), .C2(PC_AS_OUT[2]),
    .C3(PC_AS_OUT[3]), .C4(PC_AS_OUT[4]));  // open: A5, B5, A6, B6, A7, B7, A8, B8, A9, B9, COUT, C5, C6, C7, C8, C9

  // Notes on the sheet:
  //   B
  //   A
endmodule

module PC (
  input  CLOCK,
  input  SELECTOR,
  input  [4:0] INPUT,
  output [4:0] OUTPUT
);

  wire multiplexer_1_out, multiplexer_2_out, multiplexer_3_out, multiplexer_4_out, multiplexer_5_out;

  Multiplexer multiplexer_1 (.in0(OUTPUT[0]), .in1(INPUT[0]), .out(multiplexer_1_out), .sel(SELECTOR));  // open: en
  Multiplexer multiplexer_2 (.in0(OUTPUT[1]), .in1(INPUT[1]), .out(multiplexer_2_out), .sel(SELECTOR));  // open: en
  Multiplexer multiplexer_3 (.in0(OUTPUT[2]), .in1(INPUT[2]), .out(multiplexer_3_out), .sel(SELECTOR));  // open: en
  Multiplexer multiplexer_4 (.in0(OUTPUT[3]), .in1(INPUT[3]), .out(multiplexer_4_out), .sel(SELECTOR));  // open: en
  Multiplexer multiplexer_5 (.in0(OUTPUT[4]), .in1(INPUT[4]), .out(multiplexer_5_out), .sel(SELECTOR));  // open: en
  D_Flip_Flop B0 (.clk(CLOCK), .D(multiplexer_1_out), .Q(OUTPUT[0]));  // open: Qn, preset, en, reset
  D_Flip_Flop B1 (.clk(CLOCK), .D(multiplexer_2_out), .Q(OUTPUT[1]));  // open: Qn, preset, en, reset
  D_Flip_Flop B2 (.clk(CLOCK), .D(multiplexer_3_out), .Q(OUTPUT[2]));  // open: Qn, preset, en, reset
  D_Flip_Flop B3 (.clk(CLOCK), .D(multiplexer_4_out), .Q(OUTPUT[3]));  // open: Qn, preset, en, reset
  D_Flip_Flop B4 (.clk(CLOCK), .D(multiplexer_5_out), .Q(OUTPUT[4]));  // open: Qn, preset, en, reset
endmodule
